// Logisim project Labo5_Melly_Rouvinez.circ as structural Verilog: 4 circuits, main circuit COUNT_BASE
module COUNT_BASE (
  input  EN,
  input  CLK,
  input  in_3,
  output Q,
  output C
);

  wire xor_1_out;

  xor xor_1 (xor_1_out, Q, EN);
  and and_1 (C, Q, EN);
  D_Flip_Flop d_ff_1 (.D(xor_1_out), .clk(CLK), .Q(Q));  // open: Qn, preset, reset

  // Notes on the sheet:
  //   Attention, votre version de Logisim
  //   ne contient pas de tracker. Si vous
  //   enregistrez votre projet, toutes les
  //   informations du tracker seront
  //   définitivement effacées.
endmodule

module COUNT_ALL (
  input  in_1,
  output [3:0] out_2
);

  wire clock_1_out, count_base_1_c, count_base_2_c, count_base_3_c;

  Clock clock_1 (.out(clock_1_out));
  COUNT_BASE count_base_1 (.EN(in_1), .CLK(clock_1_out), .Q(out_2[0]), .C(count_base_1_c));  // open: in_3
  COUNT_BASE count_base_2 (.EN(count_base_1_c), .CLK(clock_1_out), .Q(out_2[1]), .C(count_base_2_c));  // open: in_3
  COUNT_BASE count_base_3 (.EN(count_base_2_c), .CLK(clock_1_out), .Q(out_2[2]), .C(count_base_3_c));  // open: in_3
  COUNT_BASE count_base_4 (.EN(count_base_3_c), .CLK(clock_1_out), .Q(out_2[3]));  // open: in_3, C

  // Notes on the sheet:
  //   Attention, votre version de Logisim
  //   ne contient pas de tracker. Si vous
  //   enregistrez votre projet, toutes les
  //   informations du tracker seront
  //   définitivement effacées.
endmodule

module SHREGI_8BITS (
  input  L,
  input  [1:0] S,
  input  [7:0] D,
  input  R,
  input  CLR,
  output [7:0] Q
);

  wire bitselector_1_out, bitselector_2_out, CLK_out;

  Clock CLK (.out(CLK_out));
  SHREGI_4BITS shregi_4bits_1 (
    .D(D[3:0]), .R(bitselector_1_out), .in_3(L), .S(S), .CLR(CLR), .CLK(CLK_out), .Q(Q[3:0]));
  SHREGI_4BITS shregi_4bits_2 (
    .D(D[7:4]), .R(R), .in_3(bitselector_2_out), .S(S), .CLR(CLR), .CLK(CLK_out), .Q(Q[7:4]));
  BitSelector #(.width(4)) bitselector_1 (.in(Q[7:4]), .out(bitselector_1_out), .sel(2'b00));
  BitSelector #(.width(4)) bitselector_2 (.in(Q[3:0]), .out(bitselector_2_out), .sel(2'b11));

  // Notes on the sheet:
  //   Attention, votre version de Logisim
  //   ne contient pas de tracker. Si vous
  //   enregistrez votre projet, toutes les
  //   informations du tracker seront
  //   définitivement effacées.
endmodule

module SHREGI_4BITS (
  input  [3:0] D,
  input  R,
  input  in_3,
  input  [1:0] S,
  input  CLR,
  input  CLK,
  output [3:0] Q
);

  wire multiplexer_1_out, multiplexer_2_out, multiplexer_3_out, multiplexer_4_out;

  Multiplexer #(.select(2), .enable("false")) multiplexer_1 (
    .in0(Q[3]), .in1(D[3]), .in2(Q[2]), .in3(R), .out(multiplexer_1_out), .sel(S));
  D_Flip_Flop d_ff_1 (.D(multiplexer_1_out), .clk(CLK), .Q(Q[3]), .reset(CLR));  // open: Qn, preset
  Multiplexer #(.select(2), .enable("false")) multiplexer_2 (
    .in0(Q[2]), .in1(D[2]), .in2(Q[1]), .in3(Q[3]), .out(multiplexer_2_out), .sel(S));
  D_Flip_Flop d_ff_2 (.D(multiplexer_2_out), .clk(CLK), .Q(Q[2]), .reset(CLR));  // open: Qn, preset
  Multiplexer #(.select(2), .enable("false")) multiplexer_3 (
    .in0(Q[1]), .in1(D[1]), .in2(Q[0]), .in3(Q[2]), .out(multiplexer_3_out), .sel(S));
  D_Flip_Flop d_ff_3 (.D(multiplexer_3_out), .clk(CLK), .Q(Q[1]), .reset(CLR));  // open: Qn, preset
  Multiplexer #(.select(2), .enable("false")) multiplexer_4 (
    .in0(Q[0]), .in1(D[0]), .in2(in_3), .in3(Q[1]), .out(multiplexer_4_out), .sel(S));
  D_Flip_Flop d_ff_4 (.D(multiplexer_4_out), .clk(CLK), .Q(Q[0]), .reset(CLR));  // open: Qn, preset

  // Notes on the sheet:
  //   Attention, votre version de Logisim
  //   ne contient pas de tracker. Si vous
  //   enregistrez votre projet, toutes les
  //   informations du tracker seront
  //   définitivement effacées.
endmodule
